// Logisim project circuit.circ as structural Verilog: 1 circuit, main circuit main
module main (
  input  E0,
  input  E1,
  input  C,
  output halt,
  output Ec
);

  wire and_1_out, and_2_out, not_1_out;

  not not_1 (not_1_out, C);
  and and_1 (and_1_out, not_1_out, E0);
  and and_2 (and_2_out, C, E1);
  or or_1 (Ec, and_1_out, and_2_out);

  assign halt = 1'b1;
endmodule
